# Fritzing sketch PIR Sensor with Arduino UNO (saved by Fritzing 0.9.4)
breadboards: 1

parts:
  DC-DC_Step-Up = IC, DIP package, 4 pins [chip_label=VMA402 part_number=VMA402]
  X1 = USB Connectors [package=usb-a-s-nosilk]
  X2 = USB Connectors [package=usb-a-s-nosilk]
  Q1 = MOSFET-NCHANNEL [part_number=IRF540N package=to220v]
  4_8v = 4 x AAA Battery Mount
  Q2 = MOSFET-NCHANNEL [part_number=IRF540N package=to220v]
  R2 = Resistor [tolerance=±5% resistance=1k package=THT]
  R3 = Resistor [tolerance=±5% resistance=10k package=THT]
  R4 = Resistor [tolerance=±5% resistance=220 package=THT]
  R5 = Resistor [tolerance=±5% resistance=220 package=THT]  # not connected
  PIR1 = PIR sensor
  Part1 = Arduino Uno (Rev3) - ICSP

nets:
  N1: DC-DC_Step-Up.pin1, 4_8v.+
  N2: DC-DC_Step-Up.pin2, 4_8v.-
  GND: DC-DC_Step-Up.pin3, X1.GND, X2.GND, Q1.S, Q2.S, R2.Pin_1, R3.Pin_1, PIR1.GND, Part1.GND
  N3: DC-DC_Step-Up.pin4, PIR1.VDD
  N4: X1.VBUS, Q1.D
  N5: X2.VBUS, Q2.D
  N6: Q1.G, R3.Pin_0, R4.Pin_0
  N7: Q2.G, R2.Pin_0
  N8: R4.Pin_1, Part1.ICSP_MISO, Part1.D12/MISO
  N9: PIR1.SIG, Part1.D2

// code stored in the sketch: Untitled.ino

int pirPin=2;
int ledPin1=13;
int ledPin2=12;
int val=0;


void setup()
{
  pinMode(pirPin,INPUT);
  pinMode(ledPin1,OUTPUT);
  pinMode(ledPin2,OUTPUT);
  Serial.begin(9600);
}

void loop()
{
  digitalWrite(ledPin1,LOW);
  digitalWrite(ledPin2,LOW);
  val = digitalRead(pirPin);
  if(val==HIGH){
    digitalWrite(ledPin1,HIGH);
    digitalWrite(ledPin2,HIGH);
    delay(1000);
    }
    else
    {
      digitalWrite(ledPin1,LOW);
      digitalWrite(ledPin2,LOW);
      
    }
}
